# Fritzing sketch ArduinoLeonardo-fw-v18Xs-ads1015 (saved by Fritzing 0.9.3b)

parts:
  Часть2 = Arduino Leonardo (Rev3b)
  Throttle_pot = Rotary Encoder [package=THT]
  Breake_pot = Rotary Encoder [package=THT]
  Clutch_pot = Rotary Encoder [package=THT]
  Handbreake_pot = Rotary Encoder [package=THT]
  ads1015_or_ads1115 = ADS1115

nets:
  N1: Часть2.D2/SDA, ads1015_or_ads1115.SDA
  N2: Часть2.D3_PWM/SCL, ads1015_or_ads1115.SCL
  N3: Часть2.5V, Throttle_pot.EncoderPinB
  N4: Часть2.GND, Throttle_pot.EncoderPinA
  N5: Часть2.A0, Throttle_pot.EncoderPinC
  N6: Часть2.A1, Breake_pot.EncoderPinC
  N7: Часть2.A2, Clutch_pot.EncoderPinC
  N8: Часть2.A3, Handbreake_pot.EncoderPinC

notes:
  10K liner pots
  Only for wirmware with option "s" (fw-v18Xs)

custom parts:
  ADS1115: ADC ADS1115
