# Fritzing sketch ArduinoLeonardoSketch (saved by Fritzing 0.9.3b)

parts:
  Часть2 = Arduino Leonardo (Rev3b)
  Throttle_pot = Rotary Encoder [package=THT]
  Breake_pot_(if_LC*_-_then_clutch_pot) = Rotary Encoder [package=THT]
  Clutch_pot_(if_LC*_-_then_handbreake_pot) = Rotary Encoder [package=THT]
  Handbreake_pot_(if_LC*_-_then_botton0) = Rotary Encoder [package=THT]
  ENCODER = YumoE6B2
  Button_3 = Round Pushbutton
  Button_4 = Round Pushbutton
  Load_Cell_Amplifer = HX711 Weighing Sensor Module  # not connected
  Load_Cell_(Weight_Sensors) = Load Cell - Red/white/black/green  # not connected

nets:
  N1: Часть2.D0/RX, ENCODER.B
  N2: Часть2.D1/TX, ENCODER.A
  N3: Часть2.D2/SDA, ENCODER.Z
  N4: Часть2.5V, Throttle_pot.EncoderPinB
  N5: Часть2.GND, Throttle_pot.EncoderPinA
  N6: Часть2.A0, Throttle_pot.EncoderPinC
  N7: Часть2.A1, Breake_pot_(if_LC*_-_then_clutch_pot).EncoderPinC
  N8: Часть2.A2, Clutch_pot_(if_LC*_-_then_handbreake_pot).EncoderPinC
  N9: Часть2.A3, Handbreake_pot_(if_LC*_-_then_botton0).EncoderPinC
  N10: Часть2.A4, Button_4.leg0
  N11: Часть2.A5, Button_3.leg0

notes:
  Button 1,2 (fw-v180 only)
  LC - load cell with HX711 (fw-w182)
  VCC
  SCK CLOCK
  DT DATA
  GND
  XH711 (fw-v182)
  A-
  A+
  E-
  E+

custom parts:
  YumoE6B2: Yumo E6B2-C incremental encoder. Resolutions 10 to 4000 pulses per revolution (depending on model number). Power from 5 to 24V (again depending on model). Dia 40mm body 30mm plus 20mm shaft.
  Load Cell - Red/white/black/green: A rectangle load cell/weighting pressure Sensor with four wires - Red, white, black, green. Normally corresponding with E+, E-, A+, A- respectively.
