# Fritzing sketch ArduinoNanoOrUno-button-box (saved by Fritzing 0.9.3b)

parts:
  Arduino_Nano/Uno = Arduino Nano (Rev3.0)
  S2 = Round Pushbutton
  S3 = Round Pushbutton
  S5 = Round Pushbutton
  S6 = Round Pushbutton
  S7 = Round Pushbutton
  S8 = Round Pushbutton
  S9 = Round Pushbutton
  S12 = Round Pushbutton
  S13 = Round Pushbutton
  S15 = Round Pushbutton
  S17 = Round Pushbutton
  Arduino_Leonardo_Micro_or_ProMicro = Arduino Leonardo (Rev3b)
  S18 = Round Pushbutton
  S19 = Round Pushbutton
  S20 = Round Pushbutton
  S21 = Round Pushbutton
  S22 = Round Pushbutton

nets:
  N1: Arduino_Nano/Uno.D1/TX, S3.leg0
  N2: Arduino_Nano/Uno.D0/RX, S6.leg0
  N3: Arduino_Nano/Uno.D2, Arduino_Leonardo_Micro_or_ProMicro.D8/A8
  N4: Arduino_Nano/Uno.D3, S9.leg0
  N5: Arduino_Nano/Uno.D4, S15.leg0
  N6: Arduino_Nano/Uno.D5, S22.leg0
  N7: Arduino_Nano/Uno.D6, S21.leg0
  N8: Arduino_Nano/Uno.D7, S19.leg0
  N9: Arduino_Nano/Uno.D8, S20.leg0
  N10: Arduino_Nano/Uno.D9, S18.leg0
  N11: Arduino_Nano/Uno.D11/MOSI, S17.leg0
  N12: Arduino_Nano/Uno.D12/MISO, Arduino_Leonardo_Micro_or_ProMicro.D6_PWM/A7
  GND: Arduino_Nano/Uno.GND, Arduino_Leonardo_Micro_or_ProMicro.GND
  5V: Arduino_Nano/Uno.5V, Arduino_Leonardo_Micro_or_ProMicro.5V
  N13: Arduino_Nano/Uno.A5, S7.leg0
  N14: Arduino_Nano/Uno.A4, S13.leg0
  N15: Arduino_Nano/Uno.A3, S12.leg0
  N16: Arduino_Nano/Uno.A2, S8.leg0
  N17: Arduino_Nano/Uno.A1, S5.leg0
  N18: Arduino_Nano/Uno.A0, S2.leg0
  N19: Arduino_Nano/Uno.D13/SCK, Arduino_Leonardo_Micro_or_ProMicro.D7

notes:
  DT
  CLK
  PL
